# Fritzing sketch CódigoLCD (saved by Fritzing 0.9.3b)

parts:
  MH-ET_LIVE_ESP32_DEVKIT1 = MH-ET LIVE ESP32 DEVKIT 38 pins
  LCD2 = LCD screen
  LCM1602_IIC2 = LCM1602 IIC [part_number="LCM1602 IIC" chip_label="LCM1602 IIC" package="DIP (Dual Inline) [THT]"]
  Matrix_keypad1 = KEYPAD 4x4
  J1 = Basic Servo
  LED1 = RGB LED (com. cathode, rgb) [package="5 mm [THT]"]

nets:
  N1: MH-ET_LIVE_ESP32_DEVKIT1.IO32, Matrix_keypad1.row4
  N2: MH-ET_LIVE_ESP32_DEVKIT1.IO33, Matrix_keypad1.row3
  N3: MH-ET_LIVE_ESP32_DEVKIT1.IO25, Matrix_keypad1.row2
  N4: MH-ET_LIVE_ESP32_DEVKIT1.IO26, Matrix_keypad1.row1
  N5: MH-ET_LIVE_ESP32_DEVKIT1.IO27, Matrix_keypad1.col4
  N6: MH-ET_LIVE_ESP32_DEVKIT1.IO14, Matrix_keypad1.col3
  N7: MH-ET_LIVE_ESP32_DEVKIT1.IO12, Matrix_keypad1.col2
  N8: MH-ET_LIVE_ESP32_DEVKIT1.IO13, Matrix_keypad1.col1
  N9: MH-ET_LIVE_ESP32_DEVKIT1.CMD, J1.gnd
  VCC: MH-ET_LIVE_ESP32_DEVKIT1.5V, LCM1602_IIC2.VCC, J1.vcc
  N10: MH-ET_LIVE_ESP32_DEVKIT1.IO22, LCM1602_IIC2.SDA
  N11: MH-ET_LIVE_ESP32_DEVKIT1.IO21, LCM1602_IIC2.SCL
  N12: MH-ET_LIVE_ESP32_DEVKIT1.IO5, J1.pulse
  N13: MH-ET_LIVE_ESP32_DEVKIT1.IO16, LED1.blue_anode
  N14: MH-ET_LIVE_ESP32_DEVKIT1.IO4, LED1.green_anode
  N15: MH-ET_LIVE_ESP32_DEVKIT1.IO15, LED1.red_anode
  N16: MH-ET_LIVE_ESP32_DEVKIT1.SD0, LED1.common_cathode
  N17: MH-ET_LIVE_ESP32_DEVKIT1.SCK, LCM1602_IIC2.GND
  VSS: LCD2.VSS, LCM1602_IIC2.VSS
  VDD: LCD2.VDD, LCM1602_IIC2.VDD
  N18: LCD2.V0, LCM1602_IIC2.V0
  N19: LCD2.RS, LCM1602_IIC2.RS
  N20: LCD2.R/W, LCM1602_IIC2.RW
  N21: LCD2.E, LCM1602_IIC2.E
  N22: LCD2.DB0, LCM1602_IIC2.D0
  N23: LCD2.DB1, LCM1602_IIC2.D1
  N24: LCD2.DB2, LCM1602_IIC2.D2
  N25: LCD2.DB3, LCM1602_IIC2.D3
  N26: LCD2.DB4, LCM1602_IIC2.D4
  N27: LCD2.DB5, LCM1602_IIC2.D5
  N28: LCD2.DB6, LCM1602_IIC2.D6
  N29: LCD2.DB7, LCM1602_IIC2.D7
  N30: LCD2.LED+, LCM1602_IIC2.A
  N31: LCD2.LED-, LCM1602_IIC2.K

custom parts:
  MH-ET LIVE ESP32 DEVKIT 38 pins: http://mh.nodebb.com/topic/2/mh-et-live-esp32-devkit
  LCM1602 IIC: I2C-Module to use a 1602 or 2004 LCD on with the wire.h libory Serial LCD Modul
  KEYPAD 4x4: Matrix keypad 16 buttons, 4 rows x 4 columns
