# Fritzing sketch CódigoSensors (saved by Fritzing 0.9.3b)

parts:
  DHT1 = DHT11 Humitidy and Temperature Sensor
  J1 = Buzzer
  MH-ET_LIVE_ESP32_DEVKIT1 = MH-ET LIVE ESP32 DEVKIT 38 pins
  Componente1 = Gas Sensor Breakout Board

nets:
  N1: DHT1.VDD, MH-ET_LIVE_ESP32_DEVKIT1.SD0
  N2: DHT1.DATA, MH-ET_LIVE_ESP32_DEVKIT1.IO2
  GND: DHT1.GND, MH-ET_LIVE_ESP32_DEVKIT1.SCK, Componente1.GND
  N3: J1.pin1, MH-ET_LIVE_ESP32_DEVKIT1.CMD
  N4: J1.pin2, MH-ET_LIVE_ESP32_DEVKIT1.IO5
  N5: MH-ET_LIVE_ESP32_DEVKIT1.5V, Componente1.B1
  N6: MH-ET_LIVE_ESP32_DEVKIT1.IO4, Componente1.H1

custom parts:
  DHT11 Humitidy and Temperature Sensor: DHT11 Humidity and Temperature Sensor
  Buzzer: Fixed frequency buzzer
  MH-ET LIVE ESP32 DEVKIT 38 pins: http://mh.nodebb.com/topic/2/mh-et-live-esp32-devkit
